// Logisim project graphics-card.circ as structural Verilog: 1 circuit, main circuit GPU Nvidia Geforce RTX 4090TI
module GPU_Nvidia_Geforce_RTX_4090TI (
  input  [3:0] apple_Y,
  input  [3:0] apple_X,
  output [15:0] row_1,
  output [15:0] row_2,
  output [15:0] row_3,
  output [15:0] row_4,
  output [15:0] row_5,
  output [15:0] row_6,
  output [15:0] row_7,
  output [15:0] row_8,
  output [15:0] row_9,
  output [15:0] row_10,
  output [15:0] row_11,
  output [15:0] row_12,
  output [15:0] row_13,
  output [15:0] row_14,
  output [15:0] row_15,
  output [15:0] row_16
);

  wire R1, R2, R3, R4, R5, R6, R7, R8, R9, R10, R11, R12, R13, R14, R15, R16;
  wire [15:0] decoder_2_out15;

  Decoder #(.select(4), .enable("false")) decoder_1 (
    .out0(R1), .out1(R2), .out2(R3), .out3(R4), .out4(R5), .out5(R6), .out6(R7), .out7(R8), .out8(R9),
    .out9(R10), .out10(R11), .out11(R12), .out12(R13), .out13(R14), .out14(R15), .out15(R16), .sel(apple_X));
  Decoder #(.select(4), .enable("false")) decoder_2 (
    .out0(decoder_2_out15[15]), .out1(decoder_2_out15[14]), .out2(decoder_2_out15[13]),
    .out3(decoder_2_out15[12]), .out4(decoder_2_out15[11]), .out5(decoder_2_out15[10]),
    .out6(decoder_2_out15[9]), .out7(decoder_2_out15[8]), .out8(decoder_2_out15[7]),
    .out9(decoder_2_out15[6]), .out10(decoder_2_out15[5]), .out11(decoder_2_out15[4]),
    .out12(decoder_2_out15[3]), .out13(decoder_2_out15[2]), .out14(decoder_2_out15[1]),
    .out15(decoder_2_out15[0]), .sel(apple_Y));
  Multiplexer #(.width(16), .enable("false")) multiplexer_1 (
    .in0({16{1'b0}}), .in1(decoder_2_out15), .out(row_1), .sel(R1));
  Multiplexer #(.width(16), .enable("false")) multiplexer_2 (
    .in0({16{1'b0}}), .in1(decoder_2_out15), .out(row_2), .sel(R2));
  Multiplexer #(.width(16), .enable("false")) multiplexer_3 (
    .in0({16{1'b0}}), .in1(decoder_2_out15), .out(row_3), .sel(R3));
  Multiplexer #(.width(16), .enable("false")) multiplexer_4 (
    .in0({16{1'b0}}), .in1(decoder_2_out15), .out(row_4), .sel(R4));
  Multiplexer #(.width(16), .enable("false")) multiplexer_5 (
    .in0({16{1'b0}}), .in1(decoder_2_out15), .out(row_5), .sel(R5));
  Multiplexer #(.width(16), .enable("false")) multiplexer_6 (
    .in0({16{1'b0}}), .in1(decoder_2_out15), .out(row_6), .sel(R6));
  Multiplexer #(.width(16), .enable("false")) multiplexer_7 (
    .in0({16{1'b0}}), .in1(decoder_2_out15), .out(row_7), .sel(R7));
  Multiplexer #(.width(16), .enable("false")) multiplexer_8 (
    .in0({16{1'b0}}), .in1(decoder_2_out15), .out(row_8), .sel(R8));
  Multiplexer #(.width(16), .enable("false")) multiplexer_9 (
    .in0({16{1'b0}}), .in1(decoder_2_out15), .out(row_9), .sel(R9));
  Multiplexer #(.width(16), .enable("false")) multiplexer_10 (
    .in0({16{1'b0}}), .in1(decoder_2_out15), .out(row_10), .sel(R10));
  Multiplexer #(.width(16), .enable("false")) multiplexer_11 (
    .in0({16{1'b0}}), .in1(decoder_2_out15), .out(row_11), .sel(R11));
  Multiplexer #(.width(16), .enable("false")) multiplexer_12 (
    .in0({16{1'b0}}), .in1(decoder_2_out15), .out(row_12), .sel(R12));
  Multiplexer #(.width(16), .enable("false")) multiplexer_13 (
    .in0({16{1'b0}}), .in1(decoder_2_out15), .out(row_13), .sel(R13));
  Multiplexer #(.width(16), .enable("false")) multiplexer_14 (
    .in0({16{1'b0}}), .in1(decoder_2_out15), .out(row_14), .sel(R14));
  Multiplexer #(.width(16), .enable("false")) multiplexer_15 (
    .in0({16{1'b0}}), .in1(decoder_2_out15), .out(row_15), .sel(R15));
  Multiplexer #(.width(16), .enable("false")) multiplexer_16 (
    .in0({16{1'b0}}), .in1(decoder_2_out15), .out(row_16), .sel(R16));
endmodule
