// Logisim project main.circ as structural Verilog: 2 circuits, main circuit main
module main (
);

  wire A_out, cdm_8_mark5_1_p2, cdm_8_mark5_1_p3, comparator_1_eq, D_out, not_1_out, not_2_out, or_1_out,
       r___w, R_out, S_out, sel, smt, tact, W_out;
  wire [1:0] multiplexer_1_out, or_2_out;
  wire [3:0] apple_X, apple_Y;
  wire [7:0] addr, cdm_8_mark5_1_p7, data_out, gpu_nvidia_geforce_rtx_4090ti_1_p1, ram_1_data;
  wire [15:0] gpu_nvidia_geforce_rtx_4090ti_1_p4, gpu_nvidia_geforce_rtx_4090ti_1_p5,
       gpu_nvidia_geforce_rtx_4090ti_1_p6, gpu_nvidia_geforce_rtx_4090ti_1_p7,
       gpu_nvidia_geforce_rtx_4090ti_1_p8, gpu_nvidia_geforce_rtx_4090ti_1_p9,
       gpu_nvidia_geforce_rtx_4090ti_1_p10, gpu_nvidia_geforce_rtx_4090ti_1_p11,
       gpu_nvidia_geforce_rtx_4090ti_1_p12, gpu_nvidia_geforce_rtx_4090ti_1_p13,
       gpu_nvidia_geforce_rtx_4090ti_1_p14, gpu_nvidia_geforce_rtx_4090ti_1_p15,
       gpu_nvidia_geforce_rtx_4090ti_1_p16, gpu_nvidia_geforce_rtx_4090ti_1_p17,
       gpu_nvidia_geforce_rtx_4090ti_1_p18, gpu_nvidia_geforce_rtx_4090ti_1_p19;

  Clock clock_1 (.out(tact));
  Multiplexer #(.width(2), .enable("false")) multiplexer_1 (
    .in0(2'b00), .in1(or_2_out), .out(multiplexer_1_out), .sel(or_1_out));
  DotMatrix #(.inputtype("row"), .matrixcols(16), .matrixrows(16)) dotmatrix_1 (
    .row0(gpu_nvidia_geforce_rtx_4090ti_1_p4), .row1(gpu_nvidia_geforce_rtx_4090ti_1_p5),
    .row2(gpu_nvidia_geforce_rtx_4090ti_1_p6), .row3(gpu_nvidia_geforce_rtx_4090ti_1_p7),
    .row4(gpu_nvidia_geforce_rtx_4090ti_1_p8), .row5(gpu_nvidia_geforce_rtx_4090ti_1_p9),
    .row6(gpu_nvidia_geforce_rtx_4090ti_1_p10), .row7(gpu_nvidia_geforce_rtx_4090ti_1_p11),
    .row8(gpu_nvidia_geforce_rtx_4090ti_1_p12), .row9(gpu_nvidia_geforce_rtx_4090ti_1_p13),
    .row10(gpu_nvidia_geforce_rtx_4090ti_1_p14), .row11(gpu_nvidia_geforce_rtx_4090ti_1_p15),
    .row12(gpu_nvidia_geforce_rtx_4090ti_1_p16), .row13(gpu_nvidia_geforce_rtx_4090ti_1_p17),
    .row14(gpu_nvidia_geforce_rtx_4090ti_1_p18), .row15(gpu_nvidia_geforce_rtx_4090ti_1_p19));
  // GPU_Nvidia_Geforce_RTX_4090TI gpu_nvidia_geforce_rtx_4090ti_1: pin names not known; wires that end beside it: gpu_nvidia_geforce_rtx_4090ti_1_p1, apple_X, apple_Y, gpu_nvidia_geforce_rtx_4090ti_1_p4, gpu_nvidia_geforce_rtx_4090ti_1_p5, gpu_nvidia_geforce_rtx_4090ti_1_p6, gpu_nvidia_geforce_rtx_4090ti_1_p7, gpu_nvidia_geforce_rtx_4090ti_1_p8, gpu_nvidia_geforce_rtx_4090ti_1_p9, gpu_nvidia_geforce_rtx_4090ti_1_p10, gpu_nvidia_geforce_rtx_4090ti_1_p11, gpu_nvidia_geforce_rtx_4090ti_1_p12, gpu_nvidia_geforce_rtx_4090ti_1_p13, gpu_nvidia_geforce_rtx_4090ti_1_p14, gpu_nvidia_geforce_rtx_4090ti_1_p15, gpu_nvidia_geforce_rtx_4090ti_1_p16, gpu_nvidia_geforce_rtx_4090ti_1_p17, gpu_nvidia_geforce_rtx_4090ti_1_p18, gpu_nvidia_geforce_rtx_4090ti_1_p19
  or or_1 (or_1_out, W_out, A_out, S_out, S_out);
  or or_2 (or_2_out[0], A_out, S_out);
  or or_3 (or_2_out[1], S_out, D_out);
  Button W (.out(W_out));
  Button A (.out(A_out));
  Button S (.out(S_out));
  Button D (.out(D_out));
  Button R (.out(R_out));
  generator_apple generator_apple_1 (.in_1(R_out), .apple_X(apple_Y));  // open: apple_Y
  generator_apple generator_apple_2 (.in_1(R_out), .apple_Y(apple_X));  // open: apple_X
  Comparator comparator_1 (.a(addr), .b(8'h90), .eq(comparator_1_eq));  // open: gt, lt
  not not_1 (not_1_out, tact);
  assign gpu_nvidia_geforce_rtx_4090ti_1_p1 = comparator_1_eq ? data_out : 8'bz;  // Controlled_Buffer controlled_buffer_1
  Decoder decoder_1 (.out0(sel), .out1(smt), .sel(cdm_8_mark5_1_p2), .en(cdm_8_mark5_1_p3));
  // CdM_8_mark5 cdm_8_mark5_1: pin names not known; wires that end beside it: tact, cdm_8_mark5_1_p2, cdm_8_mark5_1_p3, r___w, addr, data_out, cdm_8_mark5_1_p7
  not not_2 (not_2_out, r___w);
  assign cdm_8_mark5_1_p7 = r___w ? ram_1_data : 8'bz;  // Controlled_Buffer controlled_buffer_2
  RAM ram_1 (.addr(addr), .data(ram_1_data), .sel(smt), .clk(not_1_out), .ld(r___w));  // open: clr
  ROM rom_1 (.addr(addr), .data(ram_1_data), .sel(sel));
  assign ram_1_data = not_2_out ? data_out : 8'bz;  // Controlled_Buffer controlled_buffer_3

  // Notes on the sheet:
  //   contents of rom_1 (hex, n*v repeats v):
  //   d0 62 b0 0 e1 13 d1 60 b5 8d d3 f 77 ed 10 35 d2 60 a9 d1 1 71 e1 25 d1 5f b5 8d d3 f 77 ed 22 35 d2
  //   5f a9 d1 2 71 e1 36 d1 5f b5 89 5 ea 33 d1 f d2 5f a9 d1 3 71 e1 47 d1 60 b5 89 5 ea 44 d1 f d2 60
  //   a9 d0 5f b0 d1 63 b5 a4 d0 60 b0 d1 64 b5 a4 d0 63 b0 b0 d0 64 b0 b0 ee 0 0 0 1 0 f0 f1
endmodule

module generator_apple (
  input  in_1,
  output [3:0] apple_X,
  output [3:0] apple_Y
);

  wire _00_checker, and_1_out, comparator_1_eq, comparator_2_eq;
  wire [3:0] random_1_out, random_2_out, transistor_1_out, transistor_2_out;

  Random #(.width(4)) random_1 (.clk(in_1), .out(random_1_out));  // open: next, clr
  Random #(.width(4)) random_2 (.clk(in_1), .out(random_2_out));  // open: next, clr
  Transistor #(.width(4)) transistor_1 (.in(random_2_out), .out(transistor_1_out), .gate(_00_checker));
  Transistor #(.width(4)) transistor_2 (.in(random_1_out), .out(transistor_2_out), .gate(_00_checker));
  Comparator #(.width(4)) comparator_1 (.a(random_1_out), .b(random_2_out), .eq(comparator_1_eq));  // open: gt, lt
  Comparator #(.width(4)) comparator_2 (.a(random_2_out), .b(4'b0000), .eq(comparator_2_eq));  // open: gt, lt
  not not_1 (_00_checker, and_1_out);
  and and_1 (and_1_out, comparator_1_eq, comparator_2_eq);
  Transistor #(.width(4)) transistor_3 (.in(random_1_out), .out(apple_X), .gate(and_1_out));
  Adder #(.width(4)) adder_1 (.a(transistor_1_out), .b(4'b0001), .out(apple_Y));  // open: cin, cout
  Adder #(.width(4)) adder_2 (.a(transistor_2_out), .b(4'b0001), .out(apple_X));  // open: cin, cout
  Transistor #(.width(4)) transistor_4 (.in(random_2_out), .out(apple_Y), .gate(and_1_out));
endmodule
